# Fritzing sketch driverControl (saved by Fritzing 1.0.3b)
breadboards: 2

parts:
  A1 = Raspberry Pi Pico2
  MAX30102_Sensor1 = MAX30102 Oximeter and Heart-Rate Sensor [part_number=MAX30102]  # not connected
  S1 = 0.91 inch OLED I2C Display 128 x 32 Pixels
  A2 = NEO-6M GPS Module [part_number=GY-GPS6MV2]
  MOD1 = MT3608 Boost No usb
  SERVO1 = Tower Pro SG90 servo [part_number=101246]  # not connected
  VCC1 = 4 x AAA Battery Mount [internal_resistance=0.1Ω]
  Bat1 = battery_holder_single_18650
  C1 = Capacitor Polarized [package=cpol-radial-1000uf-63v]  # not connected

nets:
  GND: A1.pin_3, A1.pin_8, A1.pin_13, A1.pin_18, A1.pin_23, A1.pin_28, A1.pin_33, A1.pin_38, A1.pin_42, S1.GND, A2.GND, MOD1.IN_(-), MOD1.OUT_(-), VCC1.-, Bat1.+#0
  N1: A1.pin_6, S1.SDA
  N2: A1.pin_7, S1.SCL
  N3: A1.pin_11, A2.Rx
  N4: A1.pin_12, A2.Tx
  N5: S1.VCC, MOD1.IN_(+), Bat1.+#1
  N6: A2.Vcc, MOD1.OUT_(+)

notes:
  This capacitor should be horizontally flipped but to no surprize fritzing does not enable the option.

custom parts:
  Raspberry Pi Pico2: Raspberry Pi Pico 2W is our new $7 microcontroller board, built on RP2350: our new high-performance, secure microcontroller with on board WiFi.
  MAX30102 Oximeter and Heart-Rate Sensor: The MAX30102 is an integrated pulse oximetry and heart-rate monitor biosensor module. It includes internal LEDs, photodetectors, optical elements, and low-noise electronics with ambient light rejection. The MAX30102 operates on a single 1.8V power supply and a separate 3.3V power supply for the internal LEDs. Communication is through a I2C-compatible interface.
  NEO-6M GPS Module: GY-GPS6MV2 NEO-6M GPS Module Module based on U-blox NEO-6M GPS engine, incorporating regulator for 3.3-5V DC input, MS621FE-compatible rechargeable battery for backup and EEPROM for storing configuration settings. Links: NEO-6 series product information page NEO-6 Datasheet
  MT3608 Boost No usb: Chip- MT3608 / B6289 DC to DC step up, power booster module. With adjustable output voltage. Current- 2A . || Input voltage- 2V-24V || Output voltage- 5V-28V Input interface- Inversed polarity- NO. || Led indicator- No.
  Tower Pro SG90 servo: Original file by John De Cristofaro http://www.adafruit.com/products/1449 Adafruit Feedback Servo (Small) Edited by: e-radionica.com 28/9/2015
  battery_holder_single_18650: single 18650 battery holder
